// Logisim project Project1Given.circ as structural Verilog: 4 circuits, main circuit main
module main (
  input  in_1,
  input  in_2,
  input  in_3,
  input  in_4,
  input  Five,
  output N,
  output E,
  output [3:0] out_8
);

  wire fiveseven_1_a, fiveseven_1_b, fiveseven_1_c, fiveseven_1_d, fiveseven_1_e, fiveseven_1_f,
       fiveseven_1_g;

  Compare compare_1 (.X0(1'b1), .X1(1'b0), .X2(1'b1), .Y0(1'b1), .Y1(1'b1), .Y2(1'b1), .N(N), .E(E));
  Gray gray_1 (.B0(1'b1), .B1(1'b0), .B2(1'b1), .B3(1'b1), .G3(out_8[0]), .G2(out_8[1]), .G1(out_8[2]), .G0(out_8[3]));
  FiveSeven fiveseven_1 (
    .V(in_1), .W(in_2), .X(in_3), .Y(in_4), .Z(Five), .A(fiveseven_1_a), .B(fiveseven_1_b),
    .C(fiveseven_1_c), .D(fiveseven_1_d), .E(fiveseven_1_e), .F(fiveseven_1_f), .G(fiveseven_1_g));
  _7_Segment_Display u_7_segment_display_1 (
    .g(fiveseven_1_g), .f(fiveseven_1_f), .a(fiveseven_1_a), .b(fiveseven_1_b), .e(fiveseven_1_e),
    .d(fiveseven_1_d), .c(fiveseven_1_c));  // open: dp
endmodule

module Compare (
  input  X0,
  input  X1,
  input  X2,
  input  Y0,
  input  Y1,
  input  Y2,
  output N,
  output E
);

  wire comparator_1_eq, comparator_1_lt, comparator_2_eq, comparator_2_lt, comparator_3_eq, comparator_3_lt;

  Comparator #(.width(1)) comparator_1 (.a(X0), .b(Y0), .eq(comparator_1_eq), .lt(comparator_1_lt));  // open: gt
  Comparator #(.width(1)) comparator_2 (.a(X1), .b(Y1), .eq(comparator_2_eq), .lt(comparator_2_lt));  // open: gt
  Comparator #(.width(1)) comparator_3 (.a(X2), .b(Y2), .eq(comparator_3_eq), .lt(comparator_3_lt));  // open: gt
  or or_1 (N, comparator_1_lt, comparator_2_lt, comparator_3_lt);
  and and_1 (E, comparator_1_eq, comparator_2_eq, comparator_3_eq);
endmodule

module Gray (
  input  B0,
  input  B1,
  input  B2,
  input  B3,
  output G3,
  output G2,
  output G1,
  output G0
);

  wire AB_out, ACD_out, AnBnCn_out, AnBnDn_out, and_1_out, and_2_out, and_3_out, and_4_out, BCnDn_out,
       BnC_out, BnD_out, not_1_out, not_3_out, not_4_out;

  and ACD (ACD_out, B3, B1, B0);
  not not_1 (not_1_out, B0);
  not not_2 (G0, B1);
  not not_3 (not_3_out, B2);
  not not_4 (not_4_out, B3);
  and AB (AB_out, B3, B2);
  and BnD (BnD_out, not_3_out, B0);
  and BnC (BnC_out, not_3_out, B1);
  and BCnDn (BCnDn_out, B2, G0, not_1_out);
  and and_1 (and_1_out, G0, not_4_out);
  and and_2 (and_2_out, not_3_out, not_4_out);
  and and_3 (and_3_out, not_4_out, not_1_out);
  and AnBnCn (AnBnCn_out, G0, not_3_out, not_4_out);
  and AnBnDn (AnBnDn_out, not_1_out, not_4_out, not_3_out);
  or or_1 (G1, BnD_out, BnC_out, BCnDn_out);
  and and_4 (and_4_out, B0, B3, B2, B1);
  or or_2 (G3, and_4_out, and_1_out, and_2_out, and_3_out);
  or or_3 (G2, AnBnCn_out, AB_out, ACD_out, AnBnDn_out);
endmodule

module FiveSeven (
  input  V,
  input  W,
  input  X,
  input  Y,
  input  Z,
  output A,
  output B,
  output C,
  output D,
  output E,
  output F,
  output G
);

  // OR_Gate or_1 has open pins: in0=V, in1=W, in2=X, in3=Y, out=open
  _7_Segment_Display u_7_segment_display_1 (.g(G), .f(F), .a(A), .b(B), .e(E), .d(D), .c(C));  // open: dp
endmodule
